# Fritzing sketch micreowave_sketch (saved by Fritzing 0.9.3b)
breadboards: 1

parts:
  부품3 = Arduino Uno (Rev3)
  DHT2 = DHT11 Humitidy and Temperature Sensor
  KY-3 = Keyes Relay [package=THT]
  KY-4 = Keyes Relay [package=THT]
  M3 = DC Motor
  M4 = DC Motor
  U2 = LCD-16X2 [package=lcd-16x2]
  S7 = Pushbutton [package="[THT]"]
  S8 = Pushbutton [package="[THT]"]
  S9 = Pushbutton [package="[THT]"]
  S10 = Pushbutton [package="[THT]"]
  S11 = Pushbutton [package="[THT]"]
  S12 = Pushbutton [package="[THT]"]
  D2F2 = D2F-FL Omron Snap Action Limit Switch with Level
  J3 = Basic Servo
  LCM1602_IIC1 = LCM1602 IIC [part_number="LCM1602 IIC" chip_label="LCM1602 IIC" package="DIP (Dual Inline) [THT]"]
  S13 = Pushbutton [package="[THT]"]

nets:
  N1: 부품3.A0, KY-4.signal
  N2: 부품3.A4/SDA, LCM1602_IIC1.SDA
  N3: 부품3.A5/SCL, LCM1602_IIC1.SCL
  N4: 부품3.D8, KY-3.signal
  N5: 부품3.D9_PWM, J3.pulse
  N6: 부품3.D10_PWM/SS, S13.Pin_1, S13.Pin_2
  N7: 부품3.D11_PWM/MOSI, S7.Pin_3, S7.Pin_4
  N8: 부품3.D12/MISO, DHT2.DATA
  N9: 부품3.D2, S8.Pin_1, S8.Pin_2
  N10: 부품3.D3_PWM, S9.Pin_1, S9.Pin_2
  N11: 부품3.D4, S10.Pin_1, S10.Pin_2
  N12: 부품3.D5_PWM, S11.Pin_1, S11.Pin_2
  N13: 부품3.D6_PWM, S12.Pin_1, S12.Pin_2
  N14: 부품3.D7, D2F2.NC
  VCC: 부품3.5V, DHT2.VDD, KY-3.power, KY-3.C, KY-4.power, KY-4.C, J3.vcc, LCM1602_IIC1.VCC
  GND: 부품3.GND, DHT2.GND, KY-3.ground, KY-4.ground, M3.pin_2, M4.pin_2, S7.Pin_1, S7.Pin_2, S8.Pin_3, S8.Pin_4, S9.Pin_3, S9.Pin_4, S10.Pin_3, S10.Pin_4, S11.Pin_3, S11.Pin_4, S12.Pin_3, S12.Pin_4, D2F2.COM, J3.gnd, LCM1602_IIC1.GND, S13.Pin_3, S13.Pin_4
  N15: KY-3.NO, M3.pin_1
  N16: KY-4.NO, M4.pin_1
  VSS: U2.VSS, LCM1602_IIC1.VSS
  VDD: U2.VDD, LCM1602_IIC1.VDD
  N17: U2.VO, LCM1602_IIC1.V0
  N18: U2.RS, LCM1602_IIC1.RS
  N19: U2.R_W, LCM1602_IIC1.RW
  N20: U2.E, LCM1602_IIC1.E
  N21: U2.DB0, LCM1602_IIC1.D0
  N22: U2.DB1, LCM1602_IIC1.D1
  N23: U2.DB2, LCM1602_IIC1.D2
  N24: U2.DB3, LCM1602_IIC1.D3
  N25: U2.DB4, LCM1602_IIC1.D4
  N26: U2.DB5, LCM1602_IIC1.D5
  N27: U2.DB6, LCM1602_IIC1.D6
  N28: U2.DB7, LCM1602_IIC1.D7
  N29: U2.A, LCM1602_IIC1.A
  N30: U2.K, LCM1602_IIC1.K

notes:
  5초/15초/30초/취소/시작 모드/펌프
  펌프모터
  팬모터

custom parts:
  DHT11 Humitidy and Temperature Sensor: DHT11 Humidity and Temperature Sensor
  Keyes Relay: The Keyes 5V relay module is suitable for SCM development, home appliance control. It uses a 5V~12V TIL control signal which can control DC / AC signal.
  D2F-FL Omron Snap Action Limit Switch with Level: Snap action switch with stainless steel lever.
  LCM1602 IIC: I2C-Module to use a 1602 or 2004 LCD on with the wire.h libory Serial LCD Modul
